# Fritzing sketch deep_sleep_mrfox1200_sch (saved by Fritzing 0.8.7b)

parts:
  S3 = Pushbutton [package="[THT]"]
  LED1 = LED - 5mm [color="Red (633nm)" package="5 mm [THT]"]  # not connected
  R1 = Resistor [tolerance=±5% resistance=680 package="0805 [SMD]"]
  MKRFox1 = Arduino MKR Fox 1200
  VCC1 = Battery

nets:
  N1: S3.Pin_3, S3.Pin_4, MKRFox1.1
  N2: R1.Pin_0, MKRFox1.D2_PWM
  N3: MKRFox1.GND, VCC1.-
  N4: MKRFox1.VCC, VCC1.+
